// Logisim project ProiectCareMerge.circ as structural Verilog
module newdesign (
  input  Input_1,
  input  Input_2,
  input  start,
  input  reset,
  input  manual,
  input  t30,
  input  t40,
  input  t60,
  input  t90,
  input  r800,
  input  r1000,
  input  r1200,
  input  spalare_rapida,
  input  camasi,
  input  antialergic,
  input  culori_inchise,
  input  rufe_murdare,
  input  door,
  input  prespalare,
  input  clatire,
  output [7:0] Output_bus_1,
  output [6:0] Output_bus_2,
  output Output_1,
  output UsaBlocata,
  output Output_2,
  output Output_3,
  output Output_4,
  output Output_5,
  output Output_6,
  output Output_7,
  output Output_8,
  output Output_9
);

  wire frequencydivider_1_clk_1hz, newstarter_1_output1, newstarter_1_startmasina, not_1_out;
  wire [4:0] newstarter_1_output4;
  wire [6:0] buttonmaibun_1_v;
  wire [12:0] counter13_1_q, mux_12to1_1_o;
  wire [15:0] time_convert_1_output;

  FrequencyDivider frequencydivider_1 (.Clock(Input_2), .reset(Input_1), .clk_1hz(frequencydivider_1_clk_1hz));
  BUTTONmaibun buttonmaibun_1 (
    .reset(reset), .MANUAL(manual), .t30(t30), .t40(t40), .t60(t60), .t90(t90), .r800(r800), .r1000(r1000),
    .r1200(r1200), .SPALARE_RAPIDA(spalare_rapida), .CAMASI(camasi), .ANTIALERGIC(antialergic),
    .CULORI_INCHISE(culori_inchise), .RUFE_MURDARE(rufe_murdare), .DOOR(door), .prespalare(prespalare),
    .clatire(clatire), .v({newstarter_1_output4[3], newstarter_1_output4[4], buttonmaibun_1_v}));
  newstarter newstarter_1 (
    .v({newstarter_1_output4[3], newstarter_1_output4[4], buttonmaibun_1_v}), .door(door), .start(start),
    .output1(newstarter_1_output1), .output2(newstarter_1_output4[2]), .output3(newstarter_1_output4[1]),
    .output4(newstarter_1_output4[0]), .startmasina(newstarter_1_startmasina));
  mux_12to1 mux_12to1_1 (.enable(newstarter_1_output1), .sel(newstarter_1_output4), .o(mux_12to1_1_o));
  ProgramMasina ProgramMasina_1 (
    .v1(newstarter_1_output4[4]), .v0(newstarter_1_output4[3]), .v8(buttonmaibun_1_v[0]),
    .v7(buttonmaibun_1_v[1]), .v6(buttonmaibun_1_v[2]), .ok(newstarter_1_startmasina),
    .v5(buttonmaibun_1_v[3]), .clk(frequencydivider_1_clk_1hz), .clatiree(Output_1), .evac(Output_2),
    .heating(Output_3), .prespalare(Output_4), .alim(Output_5), .spalare(Output_6), .centri(Output_7),
    .usa(Output_8), .finalizare(Output_9));
  not not_1 (not_1_out, newstarter_1_startmasina);
  Counter13 counter13_1 (
    .Load(not_1_out), .Clk_EN(newstarter_1_startmasina), .CLK(frequencydivider_1_clk_1hz), .RST(reset),
    .Data(mux_12to1_1_o), .Q(counter13_1_q));
  time_convert time_convert_1 (.\input (counter13_1_q), .\output (time_convert_1_output));
  OR_gate or_gate_1 (
    .a(Output_1), .b(Output_8), .c(Output_2), .d(Output_3), .e(Output_4), .f(Output_5), .g(Output_6),
    .h(Output_7), .rez(UsaBlocata));
  SSD ssd_1 (
    .clk(Input_2), .d0(time_convert_1_output[15:12]), .d1(time_convert_1_output[11:8]),
    .d2(time_convert_1_output[7:4]), .d3(time_convert_1_output[3:0]), .an(Output_bus_1), .cat(Output_bus_2));
endmodule

module ProgramMasina (
  input  v1,
  input  v0,
  input  v8,
  input  v7,
  input  v6,
  input  ok,
  input  v5,
  input  clk,
  output clatiree,
  output evac,
  output heating,
  output prespalare,
  output alim,
  output spalare,
  output centri,
  output usa,
  output finalizare
);

  wire alimentare_1_fin, centrifugare_1_fin, clatire_1_fin, evacuare_1_fin, incalzire_apa_1_fin,
       prewash_1_fin, spalare_principala_1_fin;

  alimentare alimentare_1 (.ok(ok), .CLK(clk), .alim(alim), .fin(alimentare_1_fin));
  incalzire_apa incalzire_apa_1 (
    .v8(v8), .v7(v7), .v6(v6), .v5(v5), .CLK(clk), .OK(alimentare_1_fin), .fin(incalzire_apa_1_fin),
    .heating(heating));
  prewash prewash_1 (.v1(v1), .ok(incalzire_apa_1_fin), .CLK(clk), .prespal(prespalare), .fin(prewash_1_fin));
  spalare_principala spalare_principala_1 (
    .ok(prewash_1_fin), .CLK(clk), .spalare(spalare), .fin(spalare_principala_1_fin));
  clatire clatire_1 (.v0(v0), .ok(spalare_principala_1_fin), .CLK(clk), .clat(clatiree), .fin(clatire_1_fin));
  evacuare evacuare_1 (.ok(clatire_1_fin), .CLK(clk), .evac(evac), .fin(evacuare_1_fin));
  centrifugare centrifugare_1 (.ok(evacuare_1_fin), .CLK(clk), .centri(centri), .fin(centrifugare_1_fin));
  usa_blocata usa_blocata_1 (.ok(centrifugare_1_fin), .CLK(clk), .usa(usa), .fin(finalizare));
endmodule

// VHDL entity Counter13, as the project stores it:
LIBRARY ieee;
USE ieee.std_logic_1164.all;

use IEEE.STD_LOGIC_UNSIGNED.ALL;

ENTITY Counter13 IS
  PORT (
		Load, Clk_EN, CLK, RST: in std_logic;
		Data: in std_logic_vector(12 downto 0);
		Q: out std_logic_vector(12 downto 0)
  );
END Counter13;

ARCHITECTURE TypeArchitecture OF Counter13 IS

signal count: std_logic_vector(12 downto 0) := (others => '0');

BEGIN
	
	process (CLK, RST)
	begin
		if RST = '1' then
			count <= (others => '0'); -- Reset the counter to 0
		elsif rising_edge(CLK) then
			if Load = '1' then
				count <= Data;
			else 
				if Clk_EN = '1' then
					count <= count - 1;
				else
					count <= count;
				end if;
			end if;
		end if;
		
		Q <= count;
	end process;

END TypeArchitecture;

// VHDL entity SevenSegmentDecoder, as the project stores it:
library ieee;
use ieee.std_logic_1164.all;
use ieee.numeric_std.all;

entity SevenSegmentDecoder is
  port (
    Input: in std_logic_vector(15 downto 0);
    
    second,seconds,minute,minutes : out std_logic_vector(6 downto 0)

  );
end entity SevenSegmentDecoder;

architecture Behavioral of SevenSegmentDecoder is
begin

  process(Input)
    variable Value0: integer range 0 to 9;
    variable Value1: integer range 0 to 9;
    variable Value2: integer range 0 to 9;
    variable Value3: integer range 0 to 9;
  begin
    Value0 := to_integer(unsigned(Input(3 downto 0)));
    Value1 := to_integer(unsigned(Input(7 downto 4)));
    Value2 := to_integer(unsigned(Input(11 downto 8)));
    Value3 := to_integer(unsigned(Input(15 downto 12)));
    
    case Value3 is
      when 0 => second <= "1111110";
      when 1 => second <= "0110000";
      when 2 => second <= "1101101";
      when 3 => second <= "1111001";
      when 4 => second <= "0110011";
      
      when 5 => second <= "1011011";
      when 6 => second <= "1011111";
      
      when 7 => second <= "1110000";
      when 8 => second <= "1111111";
      when 9 => second <= "1111011";
      when others => second<= "-------";
    end case;
    
    case Value2 is
      when 0 => seconds <=  "1111110";
      when 1 => seconds <=  "0110000";
      when 2 => seconds <=  "1101101";
      when 3 => seconds <="1111001";
      when 4 => seconds <=  "0110011";
      when 5 => seconds <= "1011011";
      when 6 => seconds <=  "1011111";
      when 7 => seconds <= "1110000";
      when 8 => seconds <=  "1111111";
      when 9 => seconds <=  "1111011";
      when others => seconds <=  "-------";
    end case;

    
    case Value1 is
      when 0 => minute <=  "1111110";
      when 1 => minute <=  "0110000";
      when 2 => minute <=  "1101101";
      when 3 => minute <="1111001";
      when 4 => minute <=  "0110011";
      when 5 => minute <= "1011011";
      when 6 => minute <=  "1011111";
      when 7 => minute <= "1110000";
      when 8 => minute <=  "1111111";
      when 9 => minute <=  "1111011";
      when others => minute <=  "-------";
    end case;

     case Value0 is
      when 0 => minutes <=  "1111110";
      when 1 => minutes <=  "0110000";
      when 2 => minutes <=  "1101101";
      when 3 => minutes <="1111001";
      when 4 => minutes <=  "0110011";
      when 5 => minutes <= "1011011";
      when 6 => minutes <=  "1011111";
      when 7 =>  minutes <= "1110000";
      when 8 => minutes <=  "1111111";
      when 9 => minutes <=  "1111011";
      when others => minutes <=  "-------";
    end case;

   end process;
   end Behavioral;

// VHDL entity time_convert, as the project stores it:
library ieee;
use ieee.std_logic_1164.all;
use ieee.numeric_std.all;

entity time_convert is
  port (
    input : in std_logic_vector(12 downto 0);
    output : out std_logic_vector(15 downto 0)
  );
end time_convert;

architecture TypeArchitecture of time_convert is
  signal minutes : integer range 0 to 70;
  signal seconds : integer range 0 to 59;
  signal num : integer := 0;
--  signal newseconds: integer range 0 to 59;
--  signal newminutes: integer range 0 to 70;

begin

  num <= to_integer(unsigned(input));
  minutes <= num / 60; 
  seconds <= num rem 60;

  process (seconds,minutes,input)
  
  variable temp_seconds: integer := 0;
  variable temp_minutes: integer :=0;
  variable BCD:std_logic_vector(15 downto 0);
  
  begin
  if seconds =0 and minutes =0 then output <= "0000000000000000" ; 
  else
  if seconds = 0 then
      temp_seconds := 59;
      temp_minutes := minutes -1;
    else 
      temp_seconds := seconds;
      temp_minutes := minutes;
    end if;
  end if;
--newseconds <= temp_seconds;
--newminutes <= temp_minutes;
 BCD (3 downto 0) := std_logic_vector (to_unsigned( temp_seconds rem 10,4));
 BCD (7 downto 4) :=std_logic_vector (to_unsigned( temp_seconds /10 ,4 )); 
 BCD (11 downto 8) := std_logic_vector (to_unsigned( temp_minutes rem 10,4));
 BCD (15 downto 12) :=std_logic_vector (to_unsigned( temp_minutes /10 ,4 ));

 output<=bcd;
  end process;
  
  
end TypeArchitecture;

// VHDL entity not_gate, as the project stores it:
-----------------------------------------------

LIBRARY ieee;
USE ieee.std_logic_1164.all;

ENTITY not_gate IS
  PORT (
  i: in std_logic;
  o :out std_logic
    );
END not_gate;


ARCHITECTURE TypeArchitecture OF not_gate IS

BEGIN

o <= not i;
END TypeArchitecture;

// VHDL entity alimentare, as the project stores it:
LIBRARY ieee;
USE ieee.std_logic_1164.all;

use IEEE.STD_LOGIC_UNSIGNED.ALL;

ENTITY alimentare IS
  PORT (
		ok, CLK: in std_logic;
		alim,fin:OUT STD_logic
  );
END alimentare;

ARCHITECTURE TypeArchitecture OF alimentare IS

signal count: std_logic_vector(3 downto 0) := (others => '0');
signal copyalim,copyfin:std_logic:='0';
signal en:std_logic:='1';

BEGIN
	
	process (CLK,ok,en)
	begin
		if ok = '1' and en='1' then
			if rising_edge(CLK) then
				count <= count+1;
				if count="1111" then
					en<='0';
					copyfin<='1';
					copyalim<='0';
				else 
					copyalim<='1';
					copyfin<='0';
				end if;
			end if;
				
		end if;
	end process;
alim<=copyalim;
fin<=copyfin;
END TypeArchitecture;

// VHDL entity incalzire_apa, as the project stores it:
LIBRARY ieee;
USE ieee.std_logic_1164.all;
use IEEE.STD_LOGIC_UNSIGNED.ALL;

ENTITY incalzire_apa IS
  PORT (
    v8, v7, v6, v5, CLK, OK : IN std_logic;
    --q:out std_logic_vector (7 downto 0);
    fin, heating: OUT std_logic
  );
END incalzire_apa;

ARCHITECTURE TypeArchitecture OF incalzire_apa IS
signal count: std_logic_vector(7 downto 0) := (others => '0');
signal en:std_logic:='1';
signal copyfin,copyheating:std_logic:='0';

BEGIN



	process (CLK,en,ok,v8,v7,v6,v5)
	begin

if v8='1' then
count <="00011110";--30
elsif v7='1' then
count <="00101101";--45
elsif v6='1' then
count <="01011010";--90
elsif v5='1' then
count<="10010110";--150
else

		if ok = '1' and en='1' then
			if rising_edge(CLK) then
				count <= count-1;
				if count="00000000" then
					en<='0';
					copyfin<='1';
					copyheating<='0';
				else 
					copyheating<='1';
					copyfin<='0';
				end if;
			end if;
				
		end if;
end if;
	end process;
heating<=copyheating;
fin<=copyfin;
--q<=count;
END TypeArchitecture;

// VHDL entity prewash, as the project stores it:
LIBRARY ieee;
USE ieee.std_logic_1164.all;

use IEEE.STD_LOGIC_UNSIGNED.ALL;

ENTITY prewash IS
  PORT (
		v1,ok, CLK: in std_logic;
		prespal,fin:OUT STD_logic
  );
END prewash;

ARCHITECTURE TypeArchitecture OF prewash IS

signal count: std_logic_vector(9 downto 0) := "0000000000";
signal copyprespal,copyfin:std_logic:='0';
signal en:std_logic:='1';

BEGIN
	
	process (CLK,ok,en,v1)
begin
if v1='1' then
count <="0000001011";
else

		if ok = '1' and en='1' then
			if rising_edge(CLK) then
				count <= count-1;
				if count="0000000000" then
					en<='0';
					copyfin<='1';
					copyprespal<='0';
				else 
					copyprespal<='1';
					copyfin<='0';
				end if;
			end if;
		else 

		end if;
end if;
	end process;
prespal<=copyprespal;
fin<=copyfin;
END TypeArchitecture;

// VHDL entity spalare_principala, as the project stores it:
LIBRARY ieee;
USE ieee.std_logic_1164.all;

use IEEE.STD_LOGIC_UNSIGNED.ALL;

ENTITY spalare_principala IS
  PORT (
		ok, CLK: in std_logic;
		spalare,fin:OUT STD_logic
  );
END spalare_principala;

ARCHITECTURE TypeArchitecture OF spalare_principala IS

signal count: std_logic_vector(10 downto 0) := (others => '0');
signal copyspalare,copyfin:std_logic:='0';
signal en:std_logic:='1';

BEGIN
	
	process (CLK,ok,en)
	begin
		if ok = '1' and en='1' then
			if rising_edge(CLK) then
				count <= count+1;
				if count="00000010001" then
					en<='0';
					copyfin<='1';
					copyspalare<='0';
				else 
					copyspalare<='1';
					copyfin<='0';
				end if;
			end if;
				
		end if;
	end process;
spalare<=copyspalare;
fin<=copyfin;
END TypeArchitecture;

// VHDL entity clatire, as the project stores it:
LIBRARY ieee;
USE ieee.std_logic_1164.all;

use IEEE.STD_LOGIC_UNSIGNED.ALL;

ENTITY clatire IS
  PORT (
		v0,ok, CLK: in std_logic;
		clat,fin:OUT STD_logic
  );
END clatire;

ARCHITECTURE TypeArchitecture OF clatire IS

signal count: std_logic_vector(10 downto 0) := "00000000111";
signal copyclatire,copyfin:std_logic:='0';
signal en:std_logic:='1';

BEGIN
	
	process (CLK,ok,en,v0)
begin
if v0='1' then
count<="00000001111";
else
		if ok = '1' and en='1' then
			if rising_edge(CLK) then
				count <= count-1;
				if count="00000000000" then
					en<='0';
					copyfin<='1';
					copyclatire<='0';
				else 
					copyclatire<='1';
					copyfin<='0';
				end if;
			end if;
				
		end if;
end if;
	end process;
clat<=copyclatire;
fin<=copyfin;
END TypeArchitecture;

// VHDL entity evacuare, as the project stores it:
LIBRARY ieee;
USE ieee.std_logic_1164.all;

use IEEE.STD_LOGIC_UNSIGNED.ALL;

ENTITY evacuare IS
  PORT (
		ok, CLK: in std_logic;
		evac,fin:OUT STD_logic
  );
END evacuare;

ARCHITECTURE TypeArchitecture OF evacuare IS

signal count: std_logic_vector(4 downto 0) := (others => '0');
signal copyevac,copyfin:std_logic:='0';
signal en:std_logic:='1';

BEGIN
	
	process (CLK,ok,en)
	begin
		if ok = '1' and en='1' then
			if rising_edge(CLK) then
				count <= count+1;
				if count="11110" then
					en<='0';
					copyfin<='1';
					copyevac<='0';
				else 
					copyevac<='1';
					copyfin<='0';
				end if;
			end if;
				
		end if;
	end process;
evac<=copyevac;
fin<=copyfin;
END TypeArchitecture;

// VHDL entity centrifugare, as the project stores it:
LIBRARY ieee;
USE ieee.std_logic_1164.all;

use IEEE.STD_LOGIC_UNSIGNED.ALL;

ENTITY centrifugare IS
  PORT (
		ok, CLK: in std_logic;
		centri,fin:OUT STD_logic
  );
END centrifugare;

ARCHITECTURE TypeArchitecture OF centrifugare IS

signal count: std_logic_vector(9 downto 0) := (others => '0');
signal copycentri,copyfin:std_logic:='0';
signal en:std_logic:='1';

BEGIN
	
	process (CLK,ok,en)
	begin
		if ok = '1' and en='1' then
			if rising_edge(CLK) then
				count <= count+1;
				if count="0000001000" then
					en<='0';
					copyfin<='1';
					copycentri<='0';
				else 
					copycentri<='1';
					copyfin<='0';
				end if;
			end if;
				
		end if;
	end process;
centri<=copycentri;
fin<=copyfin;
END TypeArchitecture;

// VHDL entity usa_blocata, as the project stores it:
LIBRARY ieee;
USE ieee.std_logic_1164.all;

use IEEE.STD_LOGIC_UNSIGNED.ALL;

ENTITY usa_blocata IS
  PORT (
		ok, CLK: in std_logic;
		usa,fin:OUT STD_logic
  );
END usa_blocata;

ARCHITECTURE TypeArchitecture OF usa_blocata IS

signal count: std_logic_vector(3 downto 0) := (others => '0');
signal copyusa,copyfin:std_logic:='0';
signal en:std_logic:='1';

BEGIN
	
	process (CLK,ok,en)
	begin
		if ok = '1' and en='1' then
			if rising_edge(CLK) then
				count <= count+1;
				if count="1111" then
					en<='0';
					copyfin<='1';
					copyusa<='0';
				else 
					copyusa<='1';
					copyfin<='0';
				end if;
			end if;
				
		end if;
	end process;
usa<=copyusa;
fin<=copyfin;
END TypeArchitecture;

// VHDL entity OR_gate, as the project stores it:
-------------------------------------------------------------

LIBRARY ieee;
USE ieee.std_logic_1164.all;

ENTITY OR_gate IS
  PORT (
		a,b,c,d,e,f,g,h:in std_logic;
		rez:out std_logic
    );
END OR_gate;


ARCHITECTURE TypeArchitecture OF OR_gate IS

BEGIN

rez <= a or b or c or d or e or f or g or h;

END TypeArchitecture;

// VHDL entity and_gate, as the project stores it:
LIBRARY ieee;
USE ieee.std_logic_1164.all;

ENTITY and_gate IS
  PORT (
 a,b :in std_logic;
 c: out std_logic
    );
END and_gate;


ARCHITECTURE TypeArchitecture OF and_gate IS

BEGIN
c <= a and b;

END TypeArchitecture;

// VHDL entity FrequencyDivider, as the project stores it:
LIBRARY ieee;
USE ieee.std_logic_1164.all;
use ieee.std_logic_unsigned.all;

ENTITY FrequencyDivider IS
  PORT (
Clock: in std_logic;
		reset: in std_logic;
		clk_1hz: out std_logic
    );
END FrequencyDivider;


ARCHITECTURE TypeArchitecture OF FrequencyDivider IS


BEGIN

--64 HZ
process (clock)
	variable  var: std_logic_vector  (25 downto 0) := (others =>'0');
	begin
		if rising_edge (clock) then
			if reset='1' 
				then var:=(others=>'0');
			else
				var:=var+1;
			end if;
		end if;
	clk_1hz <= var(25);
end process;

	
END TypeArchitecture;

// VHDL entity BUTTONmaibun, as the project stores it:
LIBRARY ieee;
USE ieee.std_logic_1164.all;

ENTITY BUTTONmaibun IS
  PORT (
   reset,MANUAL:in STD_LOGIC;
  t30,t40,t60,t90 :in STD_LOGIC;
  r800,r1000,r1200:in STD_LOGIC;
  SPALARE_RAPIDA,CAMASI,ANTIALERGIC,CULORI_INCHISE,RUFE_MURDARE,DOOR:in STD_LOGIC;
  prespalare,clatire :in STD_LOGIC;
  v : out STD_LOGIC_VECTOR(8 downto 0)
    );
END BUTTONmaibun;

ARCHITECTURE TypeArchitecture OF BUTTONmaibun IS
signal doorandmanual: std_logic;
signal doorandautomat: std_logic;
--signal vector:std_logic_vector (8 downto 0) := (others =>'0');
BEGIN
--process(reset,t30,t40,t60,t90,r800,r1000,r1200,prespalare,clatire,SPALARE_RAPIDA,CAMASI,ANTIALERGIC,CULORI_INCHISE,RUFE_MURDARE,DOOR,MANUAL,Anulare_Prespalare,Anulare_clatire)
--begin
doorandmanual <= door and manual;
doorandautomat <= door and (not manual);

v(0) <= ((doorandmanual and t30) or (doorandautomat and spalare_rapida)) and (not RESET) ;
v(1) <= ((doorandmanual and t40) or (doorandautomat and (culori_inchise or rufe_murdare))) and (not RESET) ;
v(2) <= ((doorandmanual and t60) or (doorandautomat and camasi)) and (not RESET) ;
v(3) <= ((doorandmanual and t90) or (doorandautomat and antialergic)) and (not RESET);
v(4) <= ((doorandmanual and r800) or (doorandautomat and camasi)) and (not RESET);
v(5) <= ((doorandmanual and r1000) or (doorandautomat and (culori_inchise or rufe_murdare)))and (not RESET)  ;
v(6) <= ((doorandmanual and r1200) or (doorandautomat and (antialergic or spalare_rapida)))and (not RESET) ;
v(7) <= ((doorandmanual and prespalare) or (doorandautomat and (rufe_murdare)))and (not RESET) ;
v(8) <= ((doorandmanual and clatire) or (doorandautomat and (culori_inchise or antialergic))) and (not RESET);


end TypeArchitecture;

// VHDL entity newstarter, as the project stores it:
LIBRARY ieee;
USE ieee.std_logic_1164.all;

ENTITY newstarter IS
  PORT (
            v: in std_logic_vector(8 downto 0);
            door,start: in std_logic;
             output1,output2,output3,output4: out std_logic;
            startmasina:out std_logic
    );
END newstarter;



ARCHITECTURE TypeArchitecture OF newstarter IS

signal doorandstart,rot,temp: std_logic;
signal signal1,signal2: std_logic;
signal b1,b2,b3,b4 :std_logic;
signal a1:std_Logic:='0';
signal en:std_logic:='1';
BEGIN


doorandstart<= door and start;
temp <= v(0) or v(1) or v(2) or v(3);
rot<= v(4) or v(5) or v(6);
signal1<= temp and rot;

signal2 <= doorandstart and signal1;




b1<= v(0) or v(1) or v(2) or v(3);
b2<= (not v(2) ) and v(3);
b3<= v(1) or v(2);
b4<= v(2) or v(0);

output1<= b1;
output2<=b2;
output3<=b3;
output4<=b4;
startmasina <= doorandstart;
END TypeArchitecture;

// VHDL entity mux_12to1, as the project stores it:
library ieee;
use ieee.std_logic_1164.all;

entity mux_12to1 is
  port (
  enable:in std_logic ;
    sel : in std_logic_vector(4 downto 0);
    o : out std_logic_vector(12 downto 0)
  );
end entity mux_12to1;

architecture behavioral of mux_12to1 is
  signal I11: std_logic_vector (12 downto 0):="0100110101011"; 
  signal I10: std_logic_vector (12 downto 0):="0110000000011";
  signal I9: std_logic_vector (12 downto 0):="0111001011011";
  
  signal I8: std_logic_vector (12 downto 0):="0100110111111";
  signal I7: std_logic_vector (12 downto 0):="0110000010111";
  signal I6: std_logic_vector (12 downto 0):="0111001101111";
  
  signal I5: std_logic_vector (12 downto 0):="0100111100111";
  signal I4: std_logic_vector (12 downto 0):="0110000111111";
  signal I3: std_logic_vector (12 downto 0):="0111010010111";
  
  signal I2: std_logic_vector (12 downto 0):="0101000100011";
  signal I1: std_logic_vector (12 downto 0):="0110001111011";
  signal I0: std_logic_vector (12 downto 0):="0111011010011";
  
  signal I: std_logic_vector (12 downto 0):= "0000000000000";
  signal copy: std_logic_vector(12 downto 0):= "0000000000000";
begin
  process (sel,enable,copy)
  begin
 if enable ='1' then
    case sel is
      when "00001" =>
        copy <= I11;
      when "01001" =>
        copy <= I10;
      when "10001" =>
        copy <= I10;
      when "11001" =>
        copy <= I9;
        
      when "00010" =>
       copy <= I8;
      when "01010" =>
        copy <= I7;
      when "10010" =>
        copy <= I7;
      when "11010" =>
        copy <= I6;
        
      when "00011" =>  
        copy <= I5;
      when "01011" =>
        copy <= I4;
      when "10011" =>
        copy <= I4;
      when "11011" =>
        copy <= I3;

      when "00100"=>
      copy <= I2;
      when "01100" =>
      copy <= I1;
      when "10100" =>
      copy <= I1;
      when "11100" =>
      copy <=I0 ;
when others =>
copy <= I;  
    end case;
    else
    copy<=I;
    end if;
      O <= copy;  
  end process;
  
end architecture behavioral;

// VHDL entity newtop, as the project stores it:
LIBRARY ieee;
USE ieee.std_logic_1164.all;

ENTITY newtop IS
  PORT (
  rst,manualt,startt ,clockt, anulare_prespalare,anulare_clatire,tt30,tt40,tt60,tt90,rr800,rr1000,rr1200,tspalare_rapida,tcamasi,tantialergic,tculori_inchise,trufe_murdare,tdoor,tprespalare,tclatire: in std_logic;
  Q: out std_logic_vector(12 downto 0)
    );
END newtop;


ARCHITECTURE TypeArchitecture1 OF newtop IS

component BUTTONmaibun IS
  PORT (
   reset,MANUAL,t30,t40,t60,t90 ,r800,r1000,r1200,SPALARE_RAPIDA,CAMASI,ANTIALERGIC,CULORI_INCHISE,RUFE_MURDARE,DOOR,prespalare,clatire :in STD_LOGIC;
  v : out STD_LOGIC_VECTOR(8 downto 0)
    );
END component;

component mux_12to1 is 
  port (
  enable:in std_logic ;
    sel : in std_logic_vector(3 downto 0);
    o : out std_logic_vector(12 downto 0)
  );
end component;

component newstarter IS
  PORT (
            v: in std_logic_vector(8 downto 0);
            door,start: in std_logic;
             output1,output2,output3,output4 : out std_logic
    );
END component;

component RegistruButtons IS
  PORT (
load,clk:in std_logic;
  		data:in std_logic_vector (8 downto 0);
  		q:out std_logic_VECTOR (8 downto 0 )

    );
END component;
component Counter13 IS
  PORT (
		Load, Clk_EN, CLK, RST: in std_logic;
		Data: in std_logic_vector(12 downto 0);
		Q: out std_logic_vector(12 downto 0)
  );
END component;
signal o1,o2,o3,o4:std_logic;
signal output_butoane,y:std_logic_vector(8 downto 0);
signal sel: std_logic_vector(3 downto 0);
signal notds,doorandstartt:std_logic;
signal output_mux,final: std_logic_vector(12 downto 0);
BEGIN


doorandstartt <= tdoor and startt;
p1:BUTTONmaibun port map (rst,manualt,tt30,tt40,tt60,tt90,rr800,rr1000,rr1200,tspalare_rapida,tcamasi,tantialergic,tculori_inchise,trufe_murdare,tdoor,tprespalare,tclatire,output_butoane) ;

--p2:RegistruButtons port map(startt,clockt,u,y);
p3:newstarter port map(output_butoane,tdoor,startt,o1,o2,o3,o4);
sel <= output_butoane(7) & output_butoane(8)& o2 & o3;
p4:mux_12to1 port map (o1 ,sel , output_mux);
notds<= not doorandstartt;
p5:counter13 port map(notds,o4,clockt,rst,output_mux,final);
Q<= final;

END TypeArchitecture1;

-----------------------------------------
LIBRARY ieee;
USE ieee.std_logic_1164.all;

ENTITY BUTTONmaibun IS
  PORT (
   reset,MANUAL:in STD_LOGIC;
  t30,t40,t60,t90 :in STD_LOGIC;
  r800,r1000,r1200:in STD_LOGIC;
  SPALARE_RAPIDA,CAMASI,ANTIALERGIC,CULORI_INCHISE,RUFE_MURDARE,DOOR:in STD_LOGIC;
  prespalare,clatire :in STD_LOGIC;
  v : out STD_LOGIC_VECTOR(8 downto 0)
    );
END BUTTONmaibun;

ARCHITECTURE TypeArchitecture2 OF BUTTONmaibun IS
signal doorandmanual: std_logic;
signal doorandautomat: std_logic;
--signal vector:std_logic_vector (8 downto 0) := (others =>'0');
BEGIN
--process(reset,t30,t40,t60,t90,r800,r1000,r1200,prespalare,clatire,SPALARE_RAPIDA,CAMASI,ANTIALERGIC,CULORI_INCHISE,RUFE_MURDARE,DOOR,MANUAL,Anulare_Prespalare,Anulare_clatire)
--begin
doorandmanual <= door and manual;
doorandautomat <= door and (not manual);

v(0) <= ((doorandmanual and t30) or (doorandautomat and spalare_rapida)) and (not RESET) ;
v(1) <= ((doorandmanual and t40) or (doorandautomat and (culori_inchise or rufe_murdare))) and (not RESET) ;
v(2) <= ((doorandmanual and t60) or (doorandautomat and camasi)) and (not RESET) ;
v(3) <= ((doorandmanual and t90) or (doorandautomat and antialergic)) and (not RESET);
v(4) <= ((doorandmanual and r800) or (doorandautomat and camasi)) and (not RESET);
v(5) <= ((doorandmanual and r1000) or (doorandautomat and (culori_inchise or rufe_murdare)))and (not RESET)  ;
v(6) <= ((doorandmanual and r1200) or (doorandautomat and (antialergic or spalare_rapida)))and (not RESET) ;
v(7) <= ((doorandmanual and prespalare) or (doorandautomat and (rufe_murdare)))and (not RESET) ;
v(8) <= ((doorandmanual and clatire) or (doorandautomat and (culori_inchise or antialergic))) and (not RESET);
end TypeArchitecture2;

library ieee;
use ieee.std_logic_1164.all;

entity mux_12to1 is
  port (
  enable:in std_logic ;
    sel : in std_logic_vector(3 downto 0);
    o : out std_logic_vector(12 downto 0)
  );
end entity mux_12to1;

architecture behavioral of mux_12to1 is
  signal I11: std_logic_vector (12 downto 0):="0111000111101";
  signal I10: std_logic_vector (12 downto 0):="0110000000011";
  signal I9: std_logic_vector (12 downto 0):="0111001011011";
  signal I8: std_logic_vector (12 downto 0):="0100110111111";
  signal I7: std_logic_vector (12 downto 0):="0110000010111";
  signal I6: std_logic_vector (12 downto 0):="0111001101111";
  signal I5: std_logic_vector (12 downto 0):="0100111100111";
  signal I4: std_logic_vector (12 downto 0):="0110000111111";
  signal I3: std_logic_vector (12 downto 0):="0111010010111";
  signal I2: std_logic_vector (12 downto 0):="0101000100011";
  signal I1: std_logic_vector (12 downto 0):="0110001111011";
  signal I0: std_logic_vector (12 downto 0):="0111011010011";
  signal I: std_logic_vector (12 downto 0):= "0000000000000";
  signal copy: std_logic_vector(12 downto 0):= "0000000000000";
begin
  process (sel,enable,copy)
  begin
 if enable ='1' then
    case sel is
      when "0000" =>
        copy <= I11;
      when "0100" =>
        copy <= I10;
      when "1000" =>
        copy <= I10;
      when "1100" =>
        copy <= I9;
        
      when "0001" =>
       copy <= I8;
      when "0101" =>
        copy <= I7;
      when "1001" =>
        copy <= I7;
      when "1101" =>
        copy <= I6;
        
      when "0010" =>  
        copy <= I5;
      when "0110" =>
        copy <= I4;
      when "1010" =>
        copy <= I4;
      when "1110" =>
        copy <= I3;

      when "0011"=>
      copy <= I2;
      when "0111" =>
      copy <= I1;
      when "1011" =>
      copy <= I1;
      when "1111" =>
      copy <=I0 ;

when others =>
copy <= I;
             O <= copy;     
    end case;
      O <= copy;  
    end if;
      O <= copy;  
  end process;
end architecture behavioral;


LIBRARY ieee;
USE ieee.std_logic_1164.all;

ENTITY newstarter IS
  PORT (
            v: in std_logic_vector(8 downto 0);
            door,start: in std_logic;
             output1,output2,output3,output4 : out std_logic
    );
END newstarter;



ARCHITECTURE TypeArchitecture OF newstarter IS

signal doorandstart,rot,temp: std_logic;
signal signal1,signal2: std_logic;
signal a1,a2,a3,b1,b2,b3 :std_logic;
BEGIN


doorandstart<= door and start;
temp <= v(0) or v(1) or v(2) or v(3);
rot<= v(4) or v(5) or v(6);
signal1<= temp and rot;
signal2 <= doorandstart and signal1;

--a1 <= v(0) and signal2;
--a2 <= v(1) and signal2;
--a3 <= v(3) and signal2;

b1<= v(0) or v(1) or v(2);
b2<= v(0) nor v(1);
b3<= v(0) nor v(2);

output1<= b1;
output2<=b2;
output3<=b3;
output4<= signal2;
END TypeArchitecture;




LIBRARY ieee;
USE ieee.std_logic_1164.all;

ENTITY RegistruButtons IS
  PORT (
load,clk:in std_logic;
  		data:in std_logic_vector (8 downto 0);
  		q:out std_logic_VECTOR (8 downto 0 )

    );
END RegistruButtons;

ARCHITECTURE TypeArchitecture4 OF RegistruButtons IS

BEGIN

	process (clk)
	variable reg: std_Logic_vector (8 downto 0) := (others => '0');
	begin
	if rising_edge(clk) then
		if (load ='1') then
			reg:=data;
		else 
			reg:=reg;
		end if;
	end if;
 q<= reg;
 end process;


END TypeArchitecture4;

LIBRARY ieee;
USE ieee.std_logic_1164.all;

use IEEE.STD_LOGIC_UNSIGNED.ALL;

ENTITY Counter13 IS
  PORT (
		Load, Clk_EN, CLK, RST: in std_logic;
		Data: in std_logic_vector(12 downto 0);
		Q: out std_logic_vector(12 downto 0)
  );
END Counter13;

ARCHITECTURE TypeArchitecture5 OF Counter13 IS

signal count: std_logic_vector(12 downto 0) := (others => '0');

BEGIN
	
	process (CLK, RST)
	begin
		if RST = '1' then
			count <= (others => '0'); -- Reset the counter to 0
		elsif rising_edge(CLK) then
			if Load = '1' then
				count <= Data;
			else 
				if Clk_EN = '1' then
					count <= count - 1;
				else
					count <= count;
				end if;
			end if;
		end if;
		
		Q <= count;
	end process;

END TypeArchitecture5;

// VHDL entity SSD, as the project stores it:
library IEEE;
use IEEE.STD_LOGIC_1164.ALL;
use IEEE.STD_LOGIC_UNSIGNED.ALL;

entity SSD is
    Port (
        clk : in STD_LOGIC;
        d0 : in STD_LOGIC_VECTOR (3 downto 0);
        d1 : in STD_LOGIC_VECTOR (3 downto 0);
        d2 : in STD_LOGIC_VECTOR (3 downto 0);
        d3 : in STD_LOGIC_VECTOR (3 downto 0);
        an : out STD_LOGIC_VECTOR (7 downto 0);
        cat : out STD_LOGIC_VECTOR (6 downto 0)
    );
end SSD;

architecture Behav of SSD is
    signal count : std_logic_vector(15 downto 0);
    signal input_decoder : std_logic_vector(3 downto 0);
begin

    -- Counter process
    process(clk, count)
    begin
        if rising_edge(clk) then
            count <= count + 1;
        end if;
    end process;

    -- ANOZI process
    process(count)
    begin
        case count(15 downto 14) is
            when "00" => an <= "00010000";
            when "01" => an <= "00100000";
            when "10" => an <= "01000000";
            when others => an <= "10000000";
        end case;
    end process;

    -- Decoder process
    process(count, d0, d1, d2, d3)
    begin
        case count(15 downto 14) is
            when "00" => input_decoder <= d0;
            when "01" => input_decoder <= d1;
            when "10" => input_decoder <= d2;
            when others => input_decoder <= d3;
        end case;
    end process;

    -- Output process
    process(input_decoder)
    begin
        case input_decoder is
      when "0000" => cat <= "1111110";
      when "0001" => cat <= "0110000";
      when "0010" => cat <= "1101101";
      when "0011" => cat <= "1111001";
      when "0100" => cat <= "0110011";
      
      when "0101" => cat <= "1011011";
      when "0110" => cat <= "1011111";
      
      when "0111" => cat <= "1110000";
      when "1000" => cat <= "1111111";
      when "1001" => cat <= "1111011";
      when others => cat <= "0000000";
        end case;
    end process;

end Behav;
